# Fritzing sketch Architecture du Prototype (saved by Fritzing 0.9.4)
circuit board: 13.1346cm x 8.04771cm
breadboards: 1

parts:
  J1 = STM32 Nucleo boards
  WeMos_D1_Mini1 = WeMos D1 Mini
  Composant1 = Adafruit VL53L0X Time of Flight Distance Sensor [part_number="Adafruit #3317"]
  LED1 = LED - 3mm [color="Red (633nm)" package="3 mm [THT]"]
  J2 = Piezo Speaker

nets:
  N1: J1.PC11, J2.pin2
  N2: J1.A4/SDA, Composant1.SDA
  N3: J1.A5/SCL, Composant1.XSHUT, Composant1.SCL
  N4: J1.D0/RX, WeMos_D1_Mini1.D2
  N5: J1.D1/TX, WeMos_D1_Mini1.D0
  3V3: J1.3V3, Composant1.VIN
  GND: J1.GND, Composant1.2.8V, Composant1.GND, LED1.cathode, J2.pin1
  N6: J1.PC10, LED1.anode

custom parts:
  Adafruit VL53L0X Time of Flight Distance Sensor: The VL53L0X is a Time of Flight distance sensor like no other you've used! The sensor contains a very tiny invisible laser source, and a matching sensor. The VL53L0X can detect the "time of flight", or how long the light has taken to bounce back to the sensor. Since it uses a very narrow light source, it is good for determining distance of only the surface directly in front of it. Unlike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
